# Fritzing sketch esp8266-TFT (saved by Fritzing 0.9.4)
breadboards: 2

parts:
  NodeMCU_v1 = NodeMCU v3 LoLin [part_number=ESP8266]
  LCD1 = TFT 1.8 inch 160x128 w SD

nets:
  N1: NodeMCU_v1.D1, LCD1.pin3
  N2: NodeMCU_v1.D2, LCD1.pin2
  N3: NodeMCU_v1.3V3, LCD1.pin_1, LCD1.pin_7
  N4: NodeMCU_v1.GND#6, NodeMCU_v1.GND#13, NodeMCU_v1.GND#16, NodeMCU_v1.GND#33, LCD1.pin_8
  N5: NodeMCU_v1.D5, LCD1.pin_6
  N6: NodeMCU_v1.D6, LCD1.pin4
  N7: NodeMCU_v1.D7, LCD1.pin_5

custom parts:
  NodeMCU v3 LoLin: NodeMCU v3 LoLin NodeMCU (http://www.nodemcu.com/) is an open source IoT platform. It includes firmware (https://nodemcu-build.com/) which runs on the ESP8266 Wi-Fi SoC from Espressif Systems, and hardware which is based on the ESP-12E module. The term "NodeMCU" by default refers to the firmware rather than the dev kits. The firmware uses the Lua scripting language. It is based on the eLua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
  TFT 1.8 inch 160x128 w SD: This is a generic 1.8 tft spi lcd display available on ebay and others. The 1.8" display has 128x160 color pixels.
